// Logisim project popcount_7seg.circ as structural Verilog: 1 circuit, main circuit main
module main (
  input  vt,
  input  en
);

  wire [1:0] adder_1_out, adder_2_out, adder_3_out, adder_4_out, adder_5_out, adder_6_out,
       bit_extender_1_out, bit_extender_2_out, bit_extender_5_out, bit_extender_6_out, bit_extender_7_out,
       bit_extender_8_out, bit_extender_9_out, bit_extender_11_out, bit_extender_12_out, bit_extender_13_out,
       bit_extender_14_out, bit_extender_15_out;
  wire [2:0] adder_7_out, adder_8_out, adder_9_out, bit_extender_16_out, bit_extender_17_out,
       bit_extender_18_out, bit_extender_19_out, bit_extender_20_out;
  wire [3:0] adder_10_out, adder_11_out, adder_12_out, bit_extender_10_out, bit_extender_21_out,
       bit_extender_22_out, bit_extender_23_out, multiplexer_1_out;
  wire [12:1] undriven;

  assign bit_extender_1_out = {{1{1'b0}}, vt};  // Bit_Extender bit_extender_1
  assign bit_extender_2_out = {{1{1'b0}}, undriven[1]};  // Bit_Extender bit_extender_2
  assign bit_extender_2_out = {{1{1'b0}}, undriven[1]};  // Bit_Extender bit_extender_3
  assign bit_extender_2_out = {{1{1'b0}}, undriven[1]};  // Bit_Extender bit_extender_4
  assign bit_extender_5_out = {{1{1'b0}}, undriven[2]};  // Bit_Extender bit_extender_5
  assign bit_extender_6_out = {{1{1'b0}}, undriven[8]};  // Bit_Extender bit_extender_6
  assign bit_extender_7_out = {{1{1'b0}}, undriven[4]};  // Bit_Extender bit_extender_7
  assign bit_extender_8_out = {{1{1'b0}}, undriven[10]};  // Bit_Extender bit_extender_8
  assign bit_extender_9_out = {{1{1'b0}}, undriven[11]};  // Bit_Extender bit_extender_9
  assign bit_extender_10_out = {{3{1'b0}}, undriven[12]};  // Bit_Extender bit_extender_10
  assign bit_extender_11_out = {{1{1'b0}}, undriven[8]};  // Bit_Extender bit_extender_11
  assign bit_extender_12_out = {{1{1'b0}}, undriven[5]};  // Bit_Extender bit_extender_12
  assign bit_extender_13_out = {{1{1'b0}}, undriven[6]};  // Bit_Extender bit_extender_13
  assign bit_extender_14_out = {{1{1'b0}}, undriven[7]};  // Bit_Extender bit_extender_14
  assign bit_extender_15_out = {{1{1'b0}}, undriven[9]};  // Bit_Extender bit_extender_15
  Adder #(.width(2)) adder_1 (
    .out(adder_1_out), .cin(bit_extender_1_out[0]), .cout(bit_extender_2_out[0]));  // open: a, b
  Adder #(.width(2)) adder_2 (
    .out(adder_2_out), .cin(bit_extender_5_out[0]), .cout(bit_extender_6_out[0]));  // open: a, b
  Adder #(.width(2)) adder_3 (
    .out(adder_3_out), .cin(bit_extender_11_out[0]), .cout(bit_extender_7_out[0]));  // open: a, b
  Adder #(.width(2)) adder_4 (
    .out(adder_4_out), .cin(bit_extender_8_out[0]), .cout(bit_extender_9_out[0]));  // open: a, b
  assign bit_extender_16_out = {{1{1'b0}}, adder_1_out};  // Bit_Extender bit_extender_16
  assign bit_extender_17_out = {{1{1'b0}}, adder_2_out};  // Bit_Extender bit_extender_17
  assign bit_extender_18_out = {{1{1'b0}}, adder_5_out};  // Bit_Extender bit_extender_18
  Adder #(.width(2)) adder_5 (
    .out(adder_5_out), .cin(bit_extender_12_out[0]), .cout(bit_extender_13_out[0]));  // open: a, b
  assign bit_extender_19_out = {{1{1'b0}}, adder_6_out};  // Bit_Extender bit_extender_19
  Adder #(.width(2)) adder_6 (
    .out(adder_6_out), .cin(bit_extender_14_out[0]), .cout(bit_extender_15_out[0]));  // open: a, b
  assign bit_extender_20_out = {{1{1'b0}}, adder_3_out};  // Bit_Extender bit_extender_20
  Adder #(.width(2)) adder_7 (
    .out(adder_7_out[1:0]), .cin(bit_extender_20_out[0]), .cout(bit_extender_18_out[0]));  // open: a, b
  Multiplexer #(.width(4)) multiplexer_1 (.in0(adder_12_out), .in1(4'b1100), .out(multiplexer_1_out), .sel(en));
  Adder #(.width(2)) adder_8 (
    .out(adder_8_out[1:0]), .cin(bit_extender_16_out[0]), .cout(bit_extender_17_out[0]));  // open: a, b
  Adder #(.width(3)) adder_9 (.out(adder_9_out), .cin(bit_extender_19_out[0]), .cout(adder_4_out[0]));  // open: a, b
  assign bit_extender_21_out = {{1{1'b0}}, adder_8_out};  // Bit_Extender bit_extender_21
  assign bit_extender_22_out = {{1{1'b0}}, adder_7_out};  // Bit_Extender bit_extender_22
  assign bit_extender_23_out = {{1{1'b0}}, adder_9_out};  // Bit_Extender bit_extender_23
  Adder #(.width(4)) adder_10 (
    .a(bit_extender_21_out), .b(bit_extender_22_out), .out(adder_10_out));  // open: cin, cout
  Adder #(.width(4)) adder_11 (
    .a(bit_extender_23_out), .b(bit_extender_10_out), .out(adder_11_out));  // open: cin, cout
  Adder #(.width(4)) adder_12 (.a(adder_10_out), .b(adder_11_out), .out(adder_12_out));  // open: cin, cout
  Hex_Digit_Display hex_digit_display_1 (.value(multiplexer_1_out));  // open: dp
  // Pins of 1 and 13 bits meet at {undriven[12:4], undriven[8], undriven[2:1], vt}
  // Pins of 1 and 2 bits meet at bit_extender_1_out
  // Pins of 1 and 2 bits meet at bit_extender_2_out
  // Pins of 1 and 2 bits meet at bit_extender_5_out
  // Pins of 1 and 2 bits meet at bit_extender_6_out
  // Pins of 1 and 2 bits meet at bit_extender_7_out
  // Pins of 1 and 2 bits meet at bit_extender_8_out
  // Pins of 1 and 2 bits meet at bit_extender_9_out
  // Pins of 1 and 2 bits meet at bit_extender_15_out
  // Pins of 1 and 2 bits meet at bit_extender_12_out
  // Pins of 1 and 2 bits meet at bit_extender_14_out
  // Pins of 1 and 2 bits meet at bit_extender_11_out
endmodule
